# Fritzing sketch klax (saved by Fritzing 1.0.5)
circuit board: 12.3cm x 5.4cm

parts:
  moto2 = female pin header, 8 pins [form="♀ (female)"]
  moto1 = female pin header, 8 pins [form="♀ (female)"]
  moto3 = female pin header, 8 pins [form="♀ (female)"]
  moto4 = female pin header, 8 pins [form="♀ (female)"]
  out = female pin header, 10 pins [form="♀ (female)"]
  in = female pin header, 2 pins [form="♀ (female)"]

nets:
  N1: moto2.pin1, moto1.pin1, moto3.pin1, moto4.pin1, out.pin1, in.pin1
  N2: moto2.pin2, moto1.pin2, moto3.pin2, moto4.pin2, out.pin2, in.pin2
  N3: moto2.pin5, out.pin7
  N4: moto2.pin7, out.pin8
  N5: moto1.pin5, out.pin10
  N6: moto1.pin7, out.pin9
  N7: moto3.pin5, out.pin6
  N8: moto3.pin7, out.pin5
  N9: moto4.pin5, out.pin3
  N10: moto4.pin7, out.pin4

notes:
  klax v0.1
  +5V
  GND
  11
  10
  9
  8
  7
  6
  5
  4
  INA4
  PWM4
  INA3
  PWM3
  PWM2
  INA2
  INA1
  PWM1
  VIN
