# Fritzing sketch klax (saved by Fritzing 0.9.10b)

parts:
  Motor_Shield_A = Monster Moto Shield
  Motor_Shield_B = Monster Moto Shield
  Arduino = Arduino UNO R4 WiFi
  BUCK_CONV = Adafruit MPM3610 5V
  12V_IN = 2.1mm Barrel Jack with Terminal Block
  MOTOR_A1 = 2.1mm Barrel Jack with Terminal Block
  MOTOR_A2 = 2.1mm Barrel Jack with Terminal Block
  MOTOR_B1 = 2.1mm Barrel Jack with Terminal Block
  MOTOR_B2 = 2.1mm Barrel Jack with Terminal Block

nets:
  N1: Motor_Shield_A.OUTA1, MOTOR_A1.POS
  N2: Motor_Shield_A.OUTB1, MOTOR_A1.NEG
  N3: Motor_Shield_A.OUTA2, MOTOR_A2.POS
  N4: Motor_Shield_A.OUTB2, MOTOR_A2.NEG
  VCC: Motor_Shield_A.VCC, Motor_Shield_B.VCC, BUCK_CONV.VIN, 12V_IN.POS
  GND: Motor_Shield_A.GND, Motor_Shield_A.GND_-_GND@0, Motor_Shield_B.GND, Motor_Shield_B.GND_-_GND@1, Motor_Shield_B.GND_-_GND@2, Arduino.Pin_10, Arduino.Pin_30, BUCK_CONV.GND, 12V_IN.NEG
  5V: Motor_Shield_A.5V, Motor_Shield_B.5V, Arduino.Pin_8, Arduino.Pin_27
  N5: Motor_Shield_A.INA2_-_D4, Arduino.Pin_38
  N6: Motor_Shield_A.PWM1_-_D5, Arduino.Pin_39
  N7: Motor_Shield_A.PWM2_-_D6, Arduino.Pin_40
  N8: Motor_Shield_A.INA1_-_D7, Arduino.Pin_41
  N9: Motor_Shield_B.OUTA1, MOTOR_B1.POS
  N10: Motor_Shield_B.OUTB1, MOTOR_B1.NEG
  N11: Motor_Shield_B.OUTA2, MOTOR_B2.POS
  N12: Motor_Shield_B.OUTB2, MOTOR_B2.NEG
  N13: Motor_Shield_B.INA2_-_D4, Arduino.Pin_42
  N14: Motor_Shield_B.PWM1_-_D5, Arduino.Pin_43
  N15: Motor_Shield_B.PWM2_-_D6, Arduino.Pin_44
  N16: Motor_Shield_B.INA1_-_D7, Arduino.Pin_45
  N17: Arduino.Pin_11, BUCK_CONV.5.0V

custom parts:
  Arduino UNO R4 WiFi: The Arduino UNO R4 WiFi merges the RA4M1 microprocessor from Renesas with the ESP32-S3 from Espressif, creating an all-in-one tool for makers with enhanced processing power and a diverse array of new peripherals.
